# Fritzing sketch EKG_SD_card_fritzing (saved by Fritzing 0.9.2b)
breadboards: 1

parts:
  IC1 = AD8232 HeartRate Monitor [part_number=SEN-12650 chip_label=IC package="DIP (Dual Inline) [THT]"]
  Componente1 = Arduino Nano (Rev3.0)
  microSD_Transflash1 = SparkFun - microSD Transflash

nets:
  GND: IC1.GND, Componente1.GND, microSD_Transflash1.GND
  3.3V: IC1.3.3v, Componente1.3V3
  N1: IC1.OUTPUT, Componente1.A0
  N2: IC1.LO-, Componente1.D6
  N3: IC1.LO+, Componente1.D5
  N4: Componente1.D10, microSD_Transflash1.CS
  N5: Componente1.D11/MOSI, microSD_Transflash1.DI
  N6: Componente1.D12/MISO, microSD_Transflash1.DO
  5V: Componente1.5V, microSD_Transflash1.VCC
  N7: Componente1.D13/SCK, microSD_Transflash1.SCK

custom parts:
  AD8232 HeartRate Monitor: A DIP stand-in part for whatever IC you want. With 10 pins on a 600mil dual inline package (DIP) footprint.
